// Logisim project maq3.circ as structural Verilog: 3 circuits, main circuit teste
module teste (
  input  reset,
  input  comprar,
  input  tipo,
  input  moeda1,
  input  moeda2,
  input  moeda3
);

  wire clock_1_out, wrap_1_dar_troco, wrap_1_emitir, wrap_1_falta_dinheiro;
  wire [3:0] wrap_1_a, wrap_1_c, wrap_1_e, wrap_1_f, wrap_1_t0, wrap_1_t1, wrap_1_t2, wrap_1_t3,
       wrap_1_tipo_cafe;

  Clock clock_1 (.out(clock_1_out));
  LED led_1 (.in(wrap_1_falta_dinheiro));
  wrap wrap_1 (
    .clock(clock_1_out), .reset(reset), .comprar(comprar), .tipo(tipo), .moeda1(moeda1), .moeda2(moeda2),
    .moeda3(moeda3), .falta_dinheiro(wrap_1_falta_dinheiro), .emitir(wrap_1_emitir),
    .dar_troco(wrap_1_dar_troco), .c(wrap_1_c), .a(wrap_1_a), .f(wrap_1_f), .e(wrap_1_e),
    .tipo_cafe(wrap_1_tipo_cafe), .T0(wrap_1_t0), .T1(wrap_1_t1), .T2(wrap_1_t2), .T3(wrap_1_t3));
  LED led_2 (.in(wrap_1_dar_troco));
  LED led_3 (.in(wrap_1_emitir));
  Hex_Digit_Display hex_digit_display_1 (.value(wrap_1_c));  // open: dp
  Hex_Digit_Display hex_digit_display_2 (.value(wrap_1_a));  // open: dp
  Hex_Digit_Display hex_digit_display_3 (.value(wrap_1_e));  // open: dp
  Hex_Digit_Display hex_digit_display_4 (.value(wrap_1_f));  // open: dp
  Hex_Digit_Display hex_digit_display_5 (.value(wrap_1_tipo_cafe));  // open: dp
  Hex_Digit_Display hex_digit_display_6 (.value(wrap_1_t2));  // open: dp
  Hex_Digit_Display hex_digit_display_7 (.value(wrap_1_t3));  // open: dp
  Hex_Digit_Display hex_digit_display_8 (.value(wrap_1_t1));  // open: dp
  Hex_Digit_Display hex_digit_display_9 (.value(wrap_1_t0));  // open: dp
endmodule

module maq (
  input  clock,
  input  tipo,
  input  moeda_3,
  input  moeda_2,
  input  moeda_1,
  input  reset,
  input  comprar,
  output [1:0] tipo_cafe,
  output falta_dinheiro,
  output emitir,
  output dar_troco,
  output [15:0] troco
);

  wire and_1_out, and_2_out, and_3_out, and_4_out, comparator_1_eq, comparator_1_gt, comparator_1_lt,
       comparator_2_eq, comparator_3_eq, comparator_4_eq, d_ff_1_q, not_1_out, not_2_out, not_3_out,
       or_1_out, or_2_out;
  wire [1:0] adder_1_out;
  wire [2:0] counter_1_q, counter_2_q, counter_3_q;
  wire [15:0] adder_2_out, multiplexer_1_out, multiplexer_2_out, multiplexer_3_out, multiplexer_4_out,
       qtd_moedas_q, register_2_q, subtractor_1_out;

  Multiplexer #(.width(16)) multiplexer_1 (
    .in0({16{1'b0}}), .in1(16'h32), .out(multiplexer_1_out), .sel(moeda_3));  // open: en
  Register #(.width(2)) register_1 (.D(adder_1_out), .en(tipo), .Q(tipo_cafe), .clk(clock));  // open: clr
  Adder #(.width(2)) adder_1 (.a(tipo_cafe), .b(2'b01), .out(adder_1_out));  // open: cin, cout
  Multiplexer #(.width(16)) multiplexer_2 (
    .in0(multiplexer_1_out), .in1(16'h64), .out(multiplexer_2_out), .sel(moeda_2));  // open: en
  Multiplexer #(.select(2), .width(16)) multiplexer_3 (
    .in0(16'hc8), .in1(16'h12c), .in2(16'h15e), .in3(16'hfa), .out(multiplexer_3_out), .sel(tipo_cafe));  // open: en
  Multiplexer #(.width(16)) multiplexer_4 (
    .in0(multiplexer_2_out), .in1(16'ha), .out(multiplexer_4_out), .sel(moeda_1));  // open: en
  Adder #(.width(16)) adder_2 (.a(multiplexer_4_out), .b(qtd_moedas_q), .out(adder_2_out));  // open: cin, cout
  Register #(.width(16)) qtd_moedas (.D(adder_2_out), .Q(qtd_moedas_q), .clk(clock), .clr(or_1_out));  // open: en
  or or_1 (or_1_out, reset, d_ff_1_q);
  Subtractor #(.width(16)) subtractor_1 (
    .a(qtd_moedas_q), .b(multiplexer_3_out), .out(subtractor_1_out));  // open: bin, bout
  Comparator #(.width(16), .mode("unsigned")) comparator_1 (
    .a(multiplexer_3_out), .b(qtd_moedas_q), .gt(comparator_1_gt), .eq(comparator_1_eq), .lt(comparator_1_lt));
  or or_2 (or_2_out, comparator_1_lt, comparator_1_eq);
  and and_1 (and_1_out, comparator_1_gt, comprar);
  and and_2 (and_2_out, or_2_out, comprar);
  Register #(.width(16)) register_2 (.D(subtractor_1_out), .en(and_4_out), .Q(register_2_q), .clk(clock));  // open: clr
  and and_3 (and_3_out, or_2_out, comprar);
  and and_4 (and_4_out, comparator_1_lt, comprar);
  D_Flip_Flop d_ff_1 (.clk(clock), .D(and_2_out), .Q(d_ff_1_q));  // open: Qn, preset, en, reset
  not not_1 (not_1_out, and_1_out);
  not not_2 (not_2_out, and_3_out);
  not not_3 (not_3_out, and_4_out);
  Counter #(.width(3), .max('h7), .ongoal("stay")) counter_1 (
    .load(and_1_out), .D(3'b000), .count(not_1_out), .Q(counter_1_q), .clk(clock));  // open: carry, clr
  Counter #(.width(3), .max('h7), .ongoal("stay")) counter_2 (
    .load(and_3_out), .D(3'b000), .count(not_2_out), .Q(counter_2_q), .clk(clock));  // open: carry, clr
  Counter #(.width(3), .max('h7), .ongoal("stay")) counter_3 (
    .load(and_4_out), .D(3'b000), .count(not_3_out), .Q(counter_3_q), .clk(clock));  // open: carry, clr
  Comparator #(.width(3)) comparator_2 (.a(counter_1_q), .b(3'b111), .eq(comparator_2_eq));  // open: gt, lt
  not not_4 (falta_dinheiro, comparator_2_eq);
  Comparator #(.width(3)) comparator_3 (.a(counter_2_q), .b(3'b111), .eq(comparator_3_eq));  // open: gt, lt
  not not_5 (emitir, comparator_3_eq);
  Comparator #(.width(3)) comparator_4 (.a(counter_3_q), .b(3'b111), .eq(comparator_4_eq));  // open: gt, lt
  not not_6 (dar_troco, comparator_4_eq);
  Multiplexer #(.width(16)) multiplexer_5 (
    .in0({16{1'b0}}), .in1(register_2_q), .out(troco), .sel(dar_troco));  // open: en
endmodule

module wrap (
  input  clock,
  input  reset,
  input  comprar,
  input  tipo,
  input  moeda1,
  input  moeda2,
  input  moeda3,
  output falta_dinheiro,
  output emitir,
  output dar_troco,
  output [3:0] c,
  output [3:0] a,
  output [3:0] f,
  output [3:0] e,
  output [3:0] tipo_cafe,
  output [3:0] T0,
  output [3:0] T1,
  output [3:0] T2,
  output [3:0] T3
);

  wire [1:0] maq_1_tipo_cafe;

  maq maq_1 (
    .clock(clock), .tipo(tipo), .moeda_3(moeda3), .moeda_2(moeda2), .moeda_1(moeda1), .reset(reset),
    .comprar(comprar), .tipo_cafe(maq_1_tipo_cafe), .falta_dinheiro(falta_dinheiro), .emitir(emitir),
    .dar_troco(dar_troco), .troco({T3, T2, T1, T0}));
  assign tipo_cafe = {{2{1'b0}}, maq_1_tipo_cafe};  // Bit_Extender bit_extender_1

  assign a = 4'b1010;
  assign c = 4'b1100;
  assign e = 4'b1110;
  assign f = 4'b1111;
endmodule
